// Logisim project 5_2_1.circ as structural Verilog: 1 circuit, main circuit main
module main (
  input  Input,
  output Inv2,
  output Inv1,
  output Inv3
);

  wire pull_resistor_3_node;

  Pull_Resistor #(.pull(1)) pull_resistor_1 (.node(Inv1));
  Transistor #(.\type ("n")) transistor_1 (.in(1'b0), .out(Inv1), .gate(Input));
  Pull_Resistor #(.pull(1)) pull_resistor_2 (.node(Inv2));
  Transistor #(.\type ("n")) transistor_2 (.in(1'b0), .out(Inv2), .gate(Inv1));
  Pull_Resistor #(.pull(1)) pull_resistor_3 (.node(pull_resistor_3_node));
  Transistor #(.\type ("n")) transistor_3 (.in(1'b0), .out(pull_resistor_3_node), .gate(Inv2));
endmodule
