// Logisim project 5_3_1d_circuit.circ as structural Verilog: 1 circuit, main circuit main
module main (
  input  A,
  input  C,
  input  B,
  output D
);

  wire transistor_1_out;

  Pull_Resistor #(.pull(1)) pull_resistor_1 (.node(D));
  Transistor #(.\type ("n")) transistor_1 (.in(1'b0), .out(transistor_1_out), .gate(C));
  Transistor #(.\type ("n")) transistor_2 (.in(1'b0), .out(transistor_1_out), .gate(A));
  Transistor #(.\type ("n")) transistor_3 (.in(1'b0), .out(D), .gate(B));
endmodule
